# Fritzing sketch schema (saved by Fritzing 0.9.5d)
breadboards: 1

parts:
  Componente1 = Arduino Uno (Rev3)
  R1 = Resistor [tolerance=±5% resistance=2k package=THT]
  R2 = Resistor [tolerance=±5% resistance=220 package=THT]
  R3 = Resistor [tolerance=±5% resistance=330 package=THT]
  R4 = Trimmer Potentiometer [maximum_resistance=10kΩ package=THT]
  R5 = Resistor [tolerance=±5% resistance=1k package=THT]

nets:
  N1: Componente1.A0, R1.Pin_0, R2.Pin_0, R5.Pin_0
  N2: Componente1.A1, R3.Pin_0, R4.wiper, R5.Pin_1
  N3: Componente1.5V, R1.Pin_1, R4.leg2
  N4: Componente1.GND, R2.Pin_1, R3.Pin_1
